// Digital circuit 74682.dig as structural Verilog
// 8-bit digiblock comparator
module _74682 (
  input  Q0,
  input  Q1,
  input  Q2,
  input  Q3,
  input  Q4,
  input  Q5,
  input  Q6,
  input  Q7,
  input  P0,
  input  P1,
  input  P2,
  input  P3,
  input  P4,
  input  P5,
  input  P6,
  input  P7,
  input  VCC,
  input  GND,
  output nP_eq_Q,
  output nP_gt_Q
);

  wire comparator_1_eq, comparator_1_gt;

  PowerSupply powersupply_1 (.VDD(VCC), .GND(GND));
  Comparator #(.Bits(8)) comparator_1 (
    .a({P7, P6, P5, P4, P3, P2, P1, P0}), .b({Q7, Q6, Q5, Q4, Q3, Q2, Q1, Q0}), .gt(comparator_1_gt),
    .eq(comparator_1_eq));  // open: lt
  not not_1 (nP_gt_Q, comparator_1_gt);
  not not_2 (nP_eq_Q, comparator_1_eq);

  // Notes on the sheet:
  //   Q0: pin 3
  //   Q1: pin 5
  //   Q2: pin 7
  //   Q3: pin 9
  //   Q4: pin 12
  //   Q5: pin 14
  //   Q6: pin 16
  //   Q7: pin 18
  //   P0: pin 2
  //   P1: pin 4
  //   P2: pin 6
  //   P3: pin 8
  //   P4: pin 11
  //   P5: pin 13
  //   P6: pin 15
  //   P7: pin 17
  //   nP_eq_Q: pin 19
  //   nP_gt_Q: pin 1
  //   VCC: pin 20, default 1
  //   GND: pin 10
endmodule

/* Test case:
P7 P6 P5 P4 P3 P2 P1 P0 Q7 Q6 Q5 Q4 Q3 Q2 Q1 Q0 ~{P=Q} ~{P>Q}
loop(P,256)
loop(Q,256)
bits(8,P) bits(8,Q) (~(P=Q)) (~(P>Q))
end loop
end loop
*/
