// Digital circuit analyzeTestTFF.dig as structural Verilog
module analyzeTestTFF (
  input  clk
);

  wire Q_0n_q;

  JK_FF Q_1n (.J(Q_0n_q), .C(clk), .K(Q_0n_q));  // open: Q, nQ
  T_FF #(.withEnable("false")) Q_0n (.C(clk), .Q(Q_0n_q));  // open: nQ
endmodule
